// Digital circuit UTS NO 12.dig as structural Verilog
module UTS_NO_12 (
  input  X,
  input  Y,
  input  Z,
  output x_2
);

  wire and_1_out, and_2_out, and_3_out, not_1_out, not_2_out;

  not not_1 (not_1_out, Y);
  not not_2 (not_2_out, Z);
  and and_1 (and_1_out, X, Y, not_1_out);
  and and_2 (and_2_out, not_1_out, not_2_out);
  and and_3 (and_3_out, X, Z);
  or or_1 (x_2, and_1_out, and_3_out, and_2_out);

  // Notes on the sheet:
  //   NAUFALFALAHHUDA
  //   XYZ'+Y'Z'+XZ
endmodule
