// Digital circuit UTS NO 13.dig as structural Verilog
module UTS_NO_13 (
  input  X,
  input  Y,
  input  Z,
  output X_2
);

  wire and_1_out, and_2_out, and_3_out, not_1_out, not_2_out, not_3_out;

  not not_1 (not_1_out, X);
  not not_2 (not_2_out, Y);
  not not_3 (not_3_out, Z);
  and and_1 (and_1_out, not_1_out, Y, Z);
  and and_2 (and_2_out, X, not_2_out);
  and and_3 (and_3_out, Y, not_3_out);
  or or_1 (X_2, and_1_out, and_2_out, and_3_out);

  // Notes on the sheet:
  //   NAUFALFALAHHUDA
  //   X'YZ+XY'+YZ'
endmodule
